# Fritzing sketch Wiring (saved by Fritzing 0.9.3b)
breadboards: 2

parts:
  Part1 = Arduino Mega 2560 (Rev3)
  Part2 = LCD1602-I2C
  S1 = KY-026
  J1 = Basic Servo
  Part3 = Thumb Joystick
  Part4 = RFID-RC522-v2
  HC-SR04_Sensor_1 = HC-SR04 Ultrasonic Distance Sensor
  Matrix_keypad1 = KEYPAD 4x4
  LED1 = 8x8 LED Matrix (blue)
  M1 = fc-51 [package=THT]
  A1 = uhppote electric strike door lock
  M2 = 1 chan 5v relay module
  HLK-PM1 = HLK-PM12 [part_number=HLK-PM12]
  PIR1 = PIR sensor

nets:
  N1: Part1.A0, S1.pin1
  N2: Part1.A1, Part3.VERT
  N3: Part1.A2, Part3.HORZ
  N4: Part1.SCL, Part2.SCL
  N5: Part1.SDA, Part2.SDA
  N6: Part1.D13_PWM, M1.pin1
  N7: Part1.D9_PWM, Part4.SDA
  N8: Part1.D8_PWM, Part4.RST
  3V3: Part1.3V3, Part4.3.3V
  GND: Part1.GND, Part4.GND
  N9: Part1.D2_PWM, J1.pulse
  N10: Part1.D3_PWM, Part3.SEL
  N11: Part1.D6_PWM, HC-SR04_Sensor_1.ECHO
  N12: Part1.D7_PWM, HC-SR04_Sensor_1.TRIG
  N13: Part1.D22, S1.pin4
  N14: Part1.D23, PIR1.SIG
  N15: Part1.D24, M2.pin_3
  N16: Part1.D29, Matrix_keypad1.col1
  N17: Part1.D31, Matrix_keypad1.col2
  N18: Part1.D33, Matrix_keypad1.col3
  N19: Part1.D35, Matrix_keypad1.col4
  N20: Part1.D37, Matrix_keypad1.row1
  N21: Part1.D39, Matrix_keypad1.row2
  N22: Part1.D41, Matrix_keypad1.row3
  N23: Part1.D43, Matrix_keypad1.row4
  N24: Part1.D50, Part4.MOSI
  N25: Part1.D51, Part4.MISO, LED1.D
  N26: Part1.D52, Part4.SCK, LED1.C
  GND_2: Part2.GND, S1.pin2, J1.gnd, Part3.GND, HC-SR04_Sensor_1.GND
  VCC: Part2.VCC, S1.pin3, J1.vcc, Part3.VCC, HC-SR04_Sensor_1.VCC
  N27: LED1.+, PIR1.VDD
  N28: LED1.-, M1.pin2, M1.pin3, PIR1.GND
  N29: A1.pin1, M2.pin_5
  N30: A1.pin2, HLK-PM1.-Vo
  N31: M2.pin_6, HLK-PM1.+Vo

custom parts:
  LCD1602-I2C: A standard character display, usually with 2x16 characters. Comes in many colors with LCM1602 IIC attached.
  KY-026: ky-026 flame sensor module
  RFID-RC522-v2: A simple China made RFID-RC522 Reader; do check the pin labels, as this is a MFRC522 based clone.
  KEYPAD 4x4: Matrix keypad 16 buttons, 4 rows x 4 columns
  8x8 LED Matrix (blue): 8x8 LED Matrix with I2C control (blue)
  uhppote electric strike door lock: UHPPOTE electric strike door lock.
  1 chan 5v relay module: 1 Channel 5V Relay Module Board Shield with Optocoupler Support High and Low Level Trigger for Arduino.
